# Fritzing sketch schema (saved by Fritzing 0.6.3b)
breadboards: 1

parts:
  Arduino1 = Arduino
  Arduino_Ethernet_Shield1 = Arduino Ethernet Shield  # not connected
  Composants1 = Breakout Board for Electret Microphone  # not connected
  S1 = Toggle Switch [package=THT]
  R1 = Resistor [tolerance=±5% resistance=10k package=THT]
  S2 = Toggle Switch [package=THT]
  R2 = Resistor [tolerance=±5% resistance=10k package=THT]
  K1 = Relay [part_number=FRS1B-S package=THT]  # not connected
  L1 = Solenoid  # not connected
  R3 = Photocell (LDR) [package=THT]  # not connected

nets:
  N1: Arduino1.D8, S1.L1, R1.Pin_1
  N2: S1.L2, S2.L2
  N3: S2.L1, R2.Pin_1
